# Fritzing sketch Wiring (saved by Fritzing 0.9.4)
circuit board: 8.46667cm x 5.64444cm
breadboards: 1

parts:
  BREAKOUT1 = ULN2003A breakout board
  BREAKOUT2 = ULN2003A breakout board
  5_V_Supply = Power plug
  HC-SR04_Sensor_1 = HC-SR04 Ultrasonic Distance Sensor
  BAT1 = Battery Holders [package=battery-aa-kit]
  R2 = Resistor [tolerance=±5% resistance=10k package="0603 [SMD]"]
  R3 = Resistor [tolerance=±5% resistance=10k package="0603 [SMD]"]
  Q1 = PHOTOTRANSISTOR REFLECTIVE OBJECT SENSOR [package=qrb1114-side]
  Q2 = PHOTOTRANSISTOR REFLECTIVE OBJECT SENSOR [package=qrb1114-side]
  Q3 = PHOTOTRANSISTOR REFLECTIVE OBJECT SENSOR [package=qrb1114-side]
  Q4 = PHOTOTRANSISTOR REFLECTIVE OBJECT SENSOR [package=qrb1114-side]
  Arduino_Uno = Arduino Uno (Rev3)
  R4 = Resistor [tolerance=±5% resistance=100 package="1206 [SMD]"]
  R6 = Resistor [tolerance=±5% resistance=100 package="1206 [SMD]"]
  R7 = Resistor [tolerance=±5% resistance=10k package="1206 [SMD]"]
  R8 = Resistor [tolerance=±5% resistance=10k package="1206 [SMD]"]
  R9 = Resistor [tolerance=±5% resistance=10k package="1206 [SMD]"]
  R10 = Resistor [tolerance=±5% resistance=10k package="1206 [SMD]"]
  Motor_supply = Power plug

nets:
  N1: BREAKOUT1.In_1, Arduino_Uno.D8
  N2: BREAKOUT1.In_2, Arduino_Uno.D9_PWM
  N3: BREAKOUT1.In_3, Arduino_Uno.D10_PWM/SS
  N4: BREAKOUT1.In_4, Arduino_Uno.D11_PWM/MOSI
  N5: BREAKOUT1.In_6, BREAKOUT1.In_7
  GND: BREAKOUT1.0V, BREAKOUT2.0V, 5_V_Supply.GND, HC-SR04_Sensor_1.GND, BAT1.-, R2.Pin_0, Q1.E, Q1.K, Q2.E, Q3.E, Q3.K, Q4.E, Arduino_Uno.GND, Motor_supply.GND
  +5V: BREAKOUT1.+5V, BREAKOUT2.+5V, Motor_supply.VCC
  N6: BREAKOUT2.In_1, Arduino_Uno.D4
  N7: BREAKOUT2.In_2, Arduino_Uno.D5_PWM
  N8: BREAKOUT2.In_3, Arduino_Uno.D6_PWM
  N9: BREAKOUT2.In_4, Arduino_Uno.D7
  VCC: 5_V_Supply.VCC, HC-SR04_Sensor_1.VCC, Arduino_Uno.5V, R7.Pin_0, R8.Pin_0, R9.Pin_0, R10.Pin_0
  N10: HC-SR04_Sensor_1.TRIG, Arduino_Uno.D3_PWM
  N11: HC-SR04_Sensor_1.ECHO, Arduino_Uno.D2
  N12: BAT1.+, R3.Pin_1
  N13: R2.Pin_1, R3.Pin_0, Arduino_Uno.A5/SCL
  N14: Q1.A, Q2.K
  N15: Q1.C, Arduino_Uno.A3, R7.Pin_1
  N16: Q2.A, R4.Pin_1
  N17: Q2.C, Arduino_Uno.A2, R8.Pin_1
  N18: Q3.A, Q4.K
  N19: Q3.C, Arduino_Uno.A1, R9.Pin_1
  N20: Q4.A, R6.Pin_1
  N21: Q4.C, Arduino_Uno.A0, R10.Pin_1
  N22: Arduino_Uno.A4/SDA, R4.Pin_0, R6.Pin_0

custom parts:
  ULN2003A breakout board: ULN2003A 7-way Darlington Transistor Driver on breakoutboard
