# Fritzing sketch Wiring (saved by Fritzing 0.9.4)
breadboards: 2

parts:
  BREAKOUT1 = ULN2003A breakout board
  BREAKOUT2 = ULN2003A breakout board
  HC-SR04_Sensor_1 = HC-SR04 Ultrasonic Distance Sensor
  R2 = Resistor [tolerance=±5% resistance=10k package="0603 [SMD]"]
  R3 = Resistor [tolerance=±5% resistance=10k package="0603 [SMD]"]
  Q1 = PHOTOTRANSISTOR REFLECTIVE OBJECT SENSOR [package=qrb1114-side]
  Q2 = PHOTOTRANSISTOR REFLECTIVE OBJECT SENSOR [package=qrb1114-side]
  Q3 = PHOTOTRANSISTOR REFLECTIVE OBJECT SENSOR [package=qrb1114-side]
  Q4 = PHOTOTRANSISTOR REFLECTIVE OBJECT SENSOR [package=qrb1114-side]
  Arduino_Uno = Arduino Uno (Rev3)
  R4 = Resistor [tolerance=±5% resistance=100 package="1206 [SMD]"]
  R6 = Resistor [tolerance=±5% resistance=100 package="1206 [SMD]"]
  R7 = Resistor [tolerance=±5% resistance=10k package="1206 [SMD]"]
  R8 = Resistor [tolerance=±5% resistance=10k package="1206 [SMD]"]
  R9 = Resistor [tolerance=±5% resistance=10k package="1206 [SMD]"]
  R10 = Resistor [tolerance=±5% resistance=10k package="1206 [SMD]"]
  U2 = LIPO-2000mAh [package=lipo-2000]
  Part1 = PowerBoost 500 Charger
  J1 = Power Jack [package=power_jack_slot]
  S1 = SPST Switch [package=switch-spdt-smd]
  MCU1 = Raspberry Pi Zero
  Q5 = Basic FET P-Channel [package="DPak [SMD]"]
  R11 = Resistor [tolerance=±5% resistance=10k package="0603 [SMD]"]
  C1 = Capacitor Polarized [package=cpol-radial-100uf-25v]
  R12 = Resistor [tolerance=±5% resistance=1.5k package="0603 [SMD]"]
  R13 = Resistor [tolerance=±5% resistance=3.3k package="0603 [SMD]"]

nets:
  N1: BREAKOUT1.In_1, Arduino_Uno.D8
  N2: BREAKOUT1.In_2, Arduino_Uno.D9_PWM
  N3: BREAKOUT1.In_3, Arduino_Uno.D10_PWM/SS
  N4: BREAKOUT1.In_4, Arduino_Uno.D11_PWM/MOSI
  GND: BREAKOUT1.0V, BREAKOUT2.0V, HC-SR04_Sensor_1.GND, R2.Pin_0, Q1.E, Q1.K, Q2.E, Q3.E, Q3.K, Q4.E, Arduino_Uno.GND, Part1.GND, J1.GND, MCU1.pin_6, MCU1.pin_9, C1.-, R13.Pin_0
  +5V: BREAKOUT1.+5V, BREAKOUT2.+5V, HC-SR04_Sensor_1.VCC, Arduino_Uno.5V, R7.Pin_0, R8.Pin_0, R9.Pin_0, R10.Pin_0, Part1.5.0V, Q5.drain, R11.Pin_1, C1.+
  N5: BREAKOUT2.In_1, Arduino_Uno.D4
  N6: BREAKOUT2.In_2, Arduino_Uno.D5_PWM
  N7: BREAKOUT2.In_3, Arduino_Uno.D6_PWM
  N8: BREAKOUT2.In_4, Arduino_Uno.D7
  N9: HC-SR04_Sensor_1.TRIG, Arduino_Uno.D3_PWM
  N10: HC-SR04_Sensor_1.ECHO, Arduino_Uno.D2
  N11: R2.Pin_1, R3.Pin_0, Arduino_Uno.A5/SCL
  N12: R3.Pin_1, Part1.VBAT_IN, S1.P
  N13: Q1.A, Q2.K
  N14: Q1.C, Arduino_Uno.A3, R7.Pin_1
  N15: Q2.A, R4.Pin_1
  N16: Q2.C, Arduino_Uno.A2, R8.Pin_1
  N17: Q3.A, Q4.K
  N18: Q3.C, Arduino_Uno.A1, R9.Pin_1
  N19: Q4.A, R6.Pin_1
  N20: Q4.C, Arduino_Uno.A0, R10.Pin_1
  N21: Arduino_Uno.A4/SDA, R4.Pin_0, R6.Pin_0
  N22: Arduino_Uno.D12/MISO, Q5.Gate, R11.Pin_0
  N23: Arduino_Uno.D13/SCK, Part1.USB, J1.PWR
  N24: Arduino_Uno.D0/RX, MCU1.pin_8
  N25: Arduino_Uno.D1/TX, R12.Pin_1
  N26: U2.+, S1.S
  N27: U2.-, Part1.GND_BAT_IN
  N28: MCU1.pin_4, Q5.source
  N29: MCU1.pin_10, R12.Pin_0, R13.Pin_1

custom parts:
  ULN2003A breakout board: ULN2003A 7-way Darlington Transistor Driver on breakoutboard
