# Fritzing sketch Wiring (saved by Fritzing 0.9.4)
circuit board: 8.46667cm x 5.64444cm

parts:
  Part1 = Arduino Ethernet Shield (Rev3)
  BREAKOUT1 = ULN2003A breakout board
  BREAKOUT2 = ULN2003A breakout board
  Power_plug1 = Power plug
  HC-SR04_Sensor_1 = HC-SR04 Ultrasonic Distance Sensor
  BAT1 = Battery Holders [package=battery-aa-kit]
  R2 = Resistor [tolerance=±5% resistance=10k package="0603 [SMD]"]
  R3 = Resistor [tolerance=±5% resistance=10k package="0603 [SMD]"]

nets:
  N1: Part1.D8, BREAKOUT1.In_1
  N2: Part1.PWM_D9, BREAKOUT1.In_2
  N3: Part1.ETH_CS, BREAKOUT1.In_3
  N4: Part1.PWM_D11, BREAKOUT1.In_4
  N5: Part1.SPI/D12, HC-SR04_Sensor_1.TRIG
  N6: Part1.SPI/D13, HC-SR04_Sensor_1.ECHO
  GND: Part1.GND, BREAKOUT1.0V, BREAKOUT2.0V, Power_plug1.GND, HC-SR04_Sensor_1.GND, BAT1.-, R2.Pin_0
  N7: Part1.A5/SCL, R2.Pin_1, R3.Pin_0
  N8: Part1.SDCS, BREAKOUT2.In_1
  N9: Part1.PWM_D5, BREAKOUT2.In_2
  N10: Part1.PWM_D6, BREAKOUT2.In_3
  N11: Part1.D7, BREAKOUT2.In_4
  5V: Part1.5V, HC-SR04_Sensor_1.VCC
  N12: BREAKOUT1.In_6, BREAKOUT1.In_7
  +5V: BREAKOUT1.+5V, BREAKOUT2.+5V, Power_plug1.VCC
  N13: BAT1.+, R3.Pin_1

custom parts:
  ULN2003A breakout board: ULN2003A 7-way Darlington Transistor Driver on breakoutboard
